# Fritzing sketch Untitled Sketch (saved by Fritzing 0.9.3b)
breadboards: 1

parts:
  부품1 = Arduino Uno (Rev3)
  hc-sr1 = hc-sr04
  LED1 = LEDs [package=led10mm]
  LED2 = LEDs [package=led10mm]
  LCD1 = LCD screen

nets:
  N1: 부품1.A4/SDA, LCD1.V0
  N2: 부품1.A5/SCL, LCD1.RS
  N3: 부품1.D12/MISO, LED1.C
  N4: 부품1.D13/SCK, LED2.C
  GND: 부품1.GND, hc-sr1.GND, LED1.A, LED2.A, LCD1.VSS
  N5: 부품1.D2, hc-sr1.Trig
  N6: 부품1.D4, hc-sr1.Echo
  5V: 부품1.5V, hc-sr1.VCC, LCD1.VDD
